# Fritzing sketch RFID collector - (Buscheck) (saved by Fritzing 1.0.5)
breadboards: 1

parts:
  Mod1 = Amica NodeMCU DEVKIT 1.0
  Componente1 = RFID-RC522-v3
  Mod2 = Passive Buzzer
  YwRobot_Power_Supply1 = YwRobot Breadboard Power Supply [part_number=545043]

nets:
  N1: Mod1.pin1, Mod1.pin_10, Mod1.pin_26, Componente1.3.3V
  N2: Mod1.pin2, Mod1.pin_9, Mod1.pin_25, Mod1.pin_29, Componente1.GND, Mod2.-, YwRobot_Power_Supply1.GND#11, YwRobot_Power_Supply1.GND#12
  N3: Mod1.pin5, Componente1.SDA
  N4: Mod1.pin6, Componente1.MOSI
  N5: Mod1.pin7, Componente1.MISO
  N6: Mod1.pin8, Componente1.SCK
  N7: Mod1.pin_11, Mod2.NC
  N8: Mod1.pin_15, Componente1.RST
  N9: Mod1.pin_30, Mod2.S, YwRobot_Power_Supply1.VCC#5, YwRobot_Power_Supply1.VCC#6
  N10: YwRobot_Power_Supply1.VCC#9, YwRobot_Power_Supply1.VCC#10
  N11: YwRobot_Power_Supply1.GND#13, YwRobot_Power_Supply1.GND#14

custom parts:
  RFID-RC522-v3: A simple China made RFID-RC522 Reader (6x4 cm); do check the pin labels, as this is a MFRC522 based clone.
  YwRobot Breadboard Power Supply: The YwRobot Breadboard Power Supply (MB-V2) has two power rails; they can be 5V or 3V3. Power to the module can be provided through the female USB socket or through the A10 (female) 2.1mm power jack.
